# Fritzing sketch Photoresistor Diagram (saved by Fritzing 0.9.4)
breadboards: 1

parts:
  Part1 = Arduino Uno (Rev3) - ICSP
  R1 = PHOTOCELL [package=photocell]
  R2 = Resistor [tolerance=±5% resistance=220 package="2512 [SMD]"]
  R3 = Resistor [tolerance=±5% resistance=220 package="2512 [SMD]"]
  LED1 = smd LED [color="Red (660nm)" package="1206 [SMD]"]
  R4 = Resistor [tolerance=±5% resistance=220 package="2512 [SMD]"]
  LED2 = smd LED [color="Green (570nm)" package="1206 [SMD]"]

nets:
  N1: Part1.A0, R1.P$2, R2.Pin_0
  N2: Part1.D8, R4.Pin_0
  N3: Part1.D9_PWM, R3.Pin_0
  N4: Part1.D13/SCK, LED1.anode
  N5: Part1.GND, R2.Pin_1, LED2.anode
  N6: Part1.5V, R1.P$1
  N7: R3.Pin_1, LED1.cathode
  N8: R4.Pin_1, LED2.cathode
